# Fritzing sketch Circuit (saved by Fritzing 0.9.3b)
breadboards: 2

parts:
  Part1 = Arduino Pro Mini v13
  U1 = RS485 [package=so08]
  U2 = RS485 [package=so08]
  U3 = attiny85 [package=dip]
  R1 = Rotary Potentiometer (Small) [maximum_resistance=100kΩ package=THT]
  J1 = Basic Servo

nets:
  GND: Part1.GND, U1._RE, U1.DE, U1.GND, U2.GND, U3.Pin_4, R1.leg2, J1.gnd
  VCC: Part1.VCC, U1.VCC, U2._RE, U2.DE, U2.VCC, U3.Pin_8, R1.leg1, J1.vcc
  N1: Part1.D9_PWM, J1.pulse
  N2: Part1.D1/RX, U1.RO
  N3: U1.A, U2.A
  N4: U1.B, U2.B
  N5: U2.DI, U3.Pin_3
  N6: U3.Pin_7, R1.wiper
